# Fritzing sketch L6203 (saved by Fritzing 0.9.3b)
breadboards: 1

parts:
  part = L6203 [chip_label=L6203 package="DIP (Dual Inline) [THT]"]
  part_2 = Ceramic Capacitor [capacitance=220nF package="100 mil [THT, multilayer]"]
  part_3 = DC Motor
  HER301 = Diode [package=diode-1n4001]
  HER301_2 = Diode [package=diode-1n4001]
  part_4 = Ceramic Capacitor [capacitance=15nF package="100 mil [THT, multilayer]"]
  part_5 = Ceramic Capacitor [capacitance=15nF package="100 mil [THT, multilayer]"]

nets:
  GND: part.SENSE, part.GND, part_2.1, HER301.A
  N1: part.BOOT2, part_4.0
  N2: part.BOOT1, part_5.0
  12V: part.Vs
  N3: part.OUT2, part_3.pin_1, HER301.C, part_4.1
  N4: part.OUT1, part_3.pin_2, HER301_2.C, part_5.1
  I/O pin: part.IN1, part.IN2
  N5: part.Vref, part_2.0, HER301_2.A
  PWM-pin: part.ENABLE

custom parts:
  L6203: A DIP stand-in part for whatever IC you want. With 12 pins on a 300mil dual inline package (DIP) footprint.
